# Fritzing sketch Tactile_Electrical Diagram (saved by Fritzing 0.9.3b)
breadboards: 3

parts:
  Part1 = Arduino Uno (Rev3)
  Power_plug1 = Power plug
  Pololu_A1 = Pololu A4988 [package=SO16]
  Part2 = Bluetooth HC-05 Macho
  DC1 = DC_DC_XL4016 [package=board_screw]
  M2 = Stepper Motor - Bipolar
  C1 = Electrolytic Capacitor [capacitance=1µF package="100 mil [THT, electrolytic]"]
  M1 = Stepper Motor - Bipolar
  Pololu_A2 = Pololu A4988 [package=SO16]
  C2 = Electrolytic Capacitor [capacitance=1µF package="100 mil [THT, electrolytic]"]

nets:
  N1: Part1.D8, Pololu_A1.ENABLE, Pololu_A2.ENABLE
  N2: Part1.D12/MISO, Part2.TXD
  N3: Part1.D13/SCK, Part2.RXD
  GND: Part1.GND, Pololu_A1.GND#8, Part2.GND, DC1.OUT-, Pololu_A2.GND#8
  N4: Part1.D2, Pololu_A1.SLEEP
  N5: Part1.D3_PWM, Pololu_A1.STEP
  N6: Part1.D4, Pololu_A1.DIR
  N7: Part1.D5_PWM, Pololu_A2.DIR
  N8: Part1.D6_PWM, Pololu_A2.STEP
  N9: Part1.D7, Pololu_A2.SLEEP
  5V: Part1.5V, Part2.VCC
  VDD: Part1.VIN, Pololu_A1.VDD, DC1.OUT+, Pololu_A2.VDD
  N10: Power_plug1.VCC, Pololu_A1.VMOT, DC1.IN+, C1.+, Pololu_A2.VMOT, C2.+
  N11: Power_plug1.GND, Pololu_A1.GND#14, DC1.IN-, C1.-, Pololu_A2.GND#14, C2.-
  N12: Pololu_A1.1B, M1.D
  N13: Pololu_A1.1A, M1.B
  N14: Pololu_A1.2A, M1.C
  N15: Pololu_A1.2B, M1.A
  N16: M2.A, Pololu_A2.2B
  N17: M2.C, Pololu_A2.2A
  N18: M2.B, Pololu_A2.1A
  N19: M2.D, Pololu_A2.1B

notes:
  12V Input
  12V to 5V buck converter
  5V Rail
  12V Rail
  Bluetooth Module
  **This is a small protoboard
